# Fritzing sketch all_components_assemble_scheme (saved by Fritzing 0.9.3b)
perfboards: 1

parts:
  MCU1 = Raspberry Pi Zero  # not connected
  J1 = shrouded pin header, 40 pins [form="♂ (shrouded male)"]
  DS1 = DS18B20 1-Wire Temperature Sensor [part_number=DS18B20]
  DS2 = DS18B20 1-Wire Temperature Sensor [part_number=DS18B20]
  DS3 = DS18B20 1-Wire Temperature Sensor [part_number=DS18B20]
  DS4 = DS18B20 1-Wire Temperature Sensor [part_number=DS18B20]
  R1 = Resistor [tolerance=±5% resistance=4.7k package=THT]

nets:
  N1: J1.pin4, DS1.DQ, DS2.DQ, DS3.DQ, DS4.DQ, R1.Pin_1
  GND: J1.pin9, DS1.GND, DS2.GND, DS3.GND, DS4.GND, R1.Pin_0
  VDD: J1.pin31, DS1.VDD, DS2.VDD, DS3.VDD, DS4.VDD
